// Logisim project 3_And_1_Combiner.circ as structural Verilog: 1 circuit, main circuit main
module main (
  input  in_1,
  input  [2:0] in_2,
  output [3:0] out_3
);

  wire [3:0] bit_extender_1_out, bit_extender_2_out, shifter_1_out, shifter_2_out;

  assign bit_extender_1_out = {{3{1'b0}}, in_1};  // Bit_Extender bit_extender_1
  assign bit_extender_2_out = {{1{1'b0}}, in_2};  // Bit_Extender bit_extender_2
  Shifter #(.width(4)) shifter_1 (.in(bit_extender_1_out), .\dist (2'b00), .out(shifter_1_out));
  Shifter #(.width(4)) shifter_2 (.in(bit_extender_2_out), .\dist (2'b01), .out(shifter_2_out));
  assign out_3 = shifter_1_out | shifter_2_out;  // OR_Gate or_1, 4 bits wide
endmodule
