// Logisim project 3_Bit_Combiner.circ as structural Verilog: 1 circuit, main circuit main
module main (
  input  right_Bit,
  input  middle_Bit,
  input  left_Bit,
  output [2:0] out_4
);

  wire [2:0] bit_extender_1_out, bit_extender_2_out, bit_extender_3_out, shifter_1_out, shifter_2_out,
       shifter_3_out;

  assign bit_extender_1_out = {{2{1'b0}}, right_Bit};  // Bit_Extender bit_extender_1
  assign bit_extender_2_out = {{2{1'b0}}, middle_Bit};  // Bit_Extender bit_extender_2
  assign bit_extender_3_out = {{2{1'b0}}, left_Bit};  // Bit_Extender bit_extender_3
  Shifter #(.width(3)) shifter_1 (.in(bit_extender_1_out), .\dist (2'b00), .out(shifter_1_out));
  Shifter #(.width(3)) shifter_2 (.in(bit_extender_2_out), .\dist (2'b01), .out(shifter_2_out));
  Shifter #(.width(3)) shifter_3 (.in(bit_extender_3_out), .\dist (2'b10), .out(shifter_3_out));
  assign out_4 = shifter_1_out | shifter_2_out | shifter_3_out;  // OR_Gate or_1, 3 bits wide
endmodule
