// Logisim project CRC.circ as structural Verilog: 4 circuits, main circuit main
module main (
  input  in_1,
  input  in_2,
  input  in_3,
  input  in_4,
  input  in_5,
  input  in_6,
  input  in_7,
  input  in_8,
  input  in_9,
  input  [3:0] Generatorpolynom,
  output [2:0] CRC
);

  wire [2:0] _3_Bit_Combiner_out_4, Muxor_2_out_3, Muxor_3_out_3, Muxor_4_out_3, Muxor_5_out_3, Muxor_out_3;
  wire [3:0] _3_And_1_Combiner_2_out_3, _3_And_1_Combiner_3_out_3, _3_And_1_Combiner_4_out_3,
       _3_And_1_Combiner_5_out_3, _3_And_1_Combiner_6_out_3, _3_And_1_Combiner_out_3;

  _3_Bit_Combiner _3_Bit_Combiner (.right_Bit(in_3), .middle_Bit(in_2), .left_Bit(in_1), .out_4(_3_Bit_Combiner_out_4));
  _3_And_1_Combiner _3_And_1_Combiner (
    .right_Bit(in_4), .left_Bits(_3_Bit_Combiner_out_4), .out_3(_3_And_1_Combiner_out_3));
  MuxXor Muxor (.Gen_Poly(Generatorpolynom), .Datenbits(_3_And_1_Combiner_out_3), .out_3(Muxor_out_3));
  _3_And_1_Combiner _3_And_1_Combiner_2 (.right_Bit(in_5), .left_Bits(Muxor_out_3), .out_3(_3_And_1_Combiner_2_out_3));
  MuxXor Muxor_2 (.Gen_Poly(Generatorpolynom), .Datenbits(_3_And_1_Combiner_2_out_3), .out_3(Muxor_2_out_3));
  _3_And_1_Combiner _3_And_1_Combiner_3 (
    .right_Bit(in_6), .left_Bits(Muxor_2_out_3), .out_3(_3_And_1_Combiner_3_out_3));
  MuxXor Muxor_3 (.Gen_Poly(Generatorpolynom), .Datenbits(_3_And_1_Combiner_3_out_3), .out_3(Muxor_3_out_3));
  _3_And_1_Combiner _3_And_1_Combiner_4 (
    .right_Bit(in_7), .left_Bits(Muxor_3_out_3), .out_3(_3_And_1_Combiner_4_out_3));
  MuxXor Muxor_4 (.Gen_Poly(Generatorpolynom), .Datenbits(_3_And_1_Combiner_4_out_3), .out_3(Muxor_4_out_3));
  _3_And_1_Combiner _3_And_1_Combiner_5 (
    .right_Bit(in_8), .left_Bits(Muxor_4_out_3), .out_3(_3_And_1_Combiner_5_out_3));
  MuxXor Muxor_5 (.Gen_Poly(Generatorpolynom), .Datenbits(_3_And_1_Combiner_5_out_3), .out_3(Muxor_5_out_3));
  _3_And_1_Combiner _3_And_1_Combiner_6 (
    .right_Bit(in_9), .left_Bits(Muxor_5_out_3), .out_3(_3_And_1_Combiner_6_out_3));
  MuxXor Muxor_6 (.Gen_Poly(Generatorpolynom), .Datenbits(_3_And_1_Combiner_6_out_3), .out_3(CRC));
endmodule

module _3_And_1_Combiner (
  input  right_Bit,
  input  [2:0] left_Bits,
  output [3:0] out_3
);

  wire [3:0] bit_extender_1_out, bit_extender_2_out, shifter_1_out, shifter_2_out;

  assign bit_extender_1_out = {{3{1'b0}}, right_Bit};  // Bit_Extender bit_extender_1
  assign bit_extender_2_out = {{1{1'b0}}, left_Bits};  // Bit_Extender bit_extender_2
  Shifter #(.width(4)) shifter_1 (.in(bit_extender_1_out), .\dist (2'b00), .out(shifter_1_out));
  Shifter #(.width(4)) shifter_2 (.in(bit_extender_2_out), .\dist (2'b01), .out(shifter_2_out));
  assign out_3 = shifter_1_out | shifter_2_out;  // OR_Gate or_1, 4 bits wide
endmodule

module _3_Bit_Combiner (
  input  right_Bit,
  input  middle_Bit,
  input  left_Bit,
  output [2:0] out_4
);

  wire [2:0] bit_extender_1_out, bit_extender_2_out, bit_extender_3_out, shifter_1_out, shifter_2_out,
       shifter_3_out;

  assign bit_extender_1_out = {{2{1'b0}}, right_Bit};  // Bit_Extender bit_extender_1
  assign bit_extender_2_out = {{2{1'b0}}, middle_Bit};  // Bit_Extender bit_extender_2
  assign bit_extender_3_out = {{2{1'b0}}, left_Bit};  // Bit_Extender bit_extender_3
  Shifter #(.width(3)) shifter_1 (.in(bit_extender_1_out), .\dist (2'b00), .out(shifter_1_out));
  Shifter #(.width(3)) shifter_2 (.in(bit_extender_2_out), .\dist (2'b01), .out(shifter_2_out));
  Shifter #(.width(3)) shifter_3 (.in(bit_extender_3_out), .\dist (2'b10), .out(shifter_3_out));
  assign out_4 = shifter_1_out | shifter_2_out | shifter_3_out;  // OR_Gate or_1, 3 bits wide
endmodule

module MuxXor (
  input  [3:0] Datenbits,
  input  [3:0] Gen_Poly,
  output [2:0] out_3
);

  wire bitselector_1_out;
  wire [3:0] multiplexer_1_out, xor_1_out;

  Multiplexer #(.width(4), .enable("false")) multiplexer_1 (
    .in0(4'b0000), .in1(Gen_Poly), .out(multiplexer_1_out), .sel(bitselector_1_out));
  BitSelector #(.width(4)) bitselector_1 (.in(Datenbits), .out(bitselector_1_out), .sel(2'b11));
  assign xor_1_out = multiplexer_1_out ^ Datenbits;  // XOR_Gate xor_1, 4 bits wide
  BitSelector #(.width(4), .group(3)) bitselector_2 (.in(xor_1_out), .out(out_3), .sel(1'b0));
endmodule
