// Logisim project Muxor_prototyp.circ as structural Verilog: 1 circuit, main circuit main
module main (
  input  [3:0] in_1,
  input  [3:0] Gen_Poly,
  output [2:0] out_3
);

  wire bitselector_1_out;
  wire [3:0] multiplexer_1_out, xor_1_out;

  Multiplexer #(.width(4), .enable("false")) multiplexer_1 (
    .in0(4'b0000), .in1(Gen_Poly), .out(multiplexer_1_out), .sel(bitselector_1_out));
  BitSelector #(.width(4)) bitselector_1 (.in(in_1), .out(bitselector_1_out), .sel(2'b11));
  assign xor_1_out = multiplexer_1_out ^ in_1;  // XOR_Gate xor_1, 4 bits wide
  BitSelector #(.width(4), .group(3)) bitselector_2 (.in(xor_1_out), .out(out_3), .sel(1'b0));
endmodule
